# Fritzing sketch ProductionPorgrammerV1 (saved by Fritzing 0.9.3b)
circuit board: 8.46667cm x 5.64444cm
breadboards: 1

parts:
  ESP2 = ESP12ESMD [part_number=ESP8266]
  Part1 = Arduino Uno (Rev3)
  R1 = Resistor [tolerance=±5% resistance=10k package=THT]
  R2 = Resistor [tolerance=±5% resistance=10k package=THT]
  R3 = Resistor [tolerance=±5% resistance=10k package=THT]
  IC1 = Voltage Regulator LM1117 [package=sot223]
  D1 = Rectifier Diode [part_number=1N4001 package="300 mil [THT]"]
  D2 = Rectifier Diode [part_number=1N4001 package="300 mil [THT]"]
  R4 = Resistor [tolerance=±5% resistance=1k package=THT]
  R5 = Resistor [tolerance=±5% resistance=1k package=THT]
  S1 = Toggle Switch [package=THT]
  Pad1 = Pad [width=11.213499157945364 height=7.0748836117566203 connect=center]

nets:
  N1: ESP2.RST, Part1.RESET
  N2: ESP2.VCC, R3.Pin_0, IC1.OUT, Pad1.pad
  GND: ESP2.GND, Part1.GND, R2.Pin_1, IC1.ADJ, D1.anode, D2.anode, S1.COM
  N3: ESP2.G15, R2.Pin_0
  N4: ESP2.G0, R1.Pin_0
  N5: ESP2.RX, D2.cathode, R4.Pin_1
  N6: ESP2.TX, D1.cathode, R5.Pin_1
  N7: ESP2.EN, R3.Pin_1
  N8: Part1.D0/RX, R4.Pin_0
  N9: Part1.D1/TX, R5.Pin_0
  N10: Part1.5V, IC1.IN
  N11: R1.Pin_1, S1.L1

custom parts:
  ESP12ESMD: Generic WiFi Module based on the ESP8266 with onboard PCB antenna and UART communications
