# Fritzing sketch ProductionPorgrammerV2 (saved by Fritzing 0.9.3b)
circuit board: 6.88566cm x 5.36311cm
breadboards: 1

parts:
  Part1 = Arduino Uno (Rev3)
  R1 = Resistor [tolerance=±5% resistance=10k package=THT]
  R2 = Resistor [tolerance=±5% resistance=10k package=THT]
  R3 = Resistor [tolerance=±5% resistance=10k package=THT]
  D1 = Rectifier Diode [part_number=1N4001 package="300 mil [THT]"]
  D2 = Rectifier Diode [part_number=1N4001 package="300 mil [THT]"]
  R4 = Resistor [tolerance=±5% resistance=1k package=THT]
  R5 = Resistor [tolerance=±5% resistance=1k package=THT]
  S1 = Toggle Switch [package=THT]
  IC1 = Voltage Regulator LM1117 [package=sot223]
  ESP2 = ESP12ESMD [part_number=ESP8266]
  Pad1 = Pad [width=11.456290682627309 height=7.5234509639756197 connect=center]  # not connected

nets:
  GND: Part1.GND, R2.Pin_1, D1.anode, D2.anode, S1.COM, IC1.ADJ, ESP2.GND
  N1: Part1.D0/RX, R4.Pin_0
  N2: Part1.D1/TX, R5.Pin_0
  N3: Part1.RESET, ESP2.RST
  N4: Part1.5V, IC1.IN
  N5: R1.Pin_0, ESP2.G0
  N6: R1.Pin_1, S1.L1
  N7: R2.Pin_0, ESP2.G15
  N8: R3.Pin_0, IC1.OUT, ESP2.VCC
  N9: R3.Pin_1, ESP2.EN
  N10: D1.cathode, R5.Pin_1, ESP2.TX
  N11: D2.cathode, R4.Pin_1, ESP2.RX

custom parts:
  ESP12ESMD: Generic WiFi Module based on the ESP8266 with onboard PCB antenna and UART communications
